// Logisim project GSHARE.circ as structural Verilog: 4 circuits, main circuit Main
module Main (
);

  wire Clock, Correct, CorrectPred, Done, gshare_predictor_1_takebranch, input_generator_1_branchtaken,
       input_generator_1_isbranch, IsPredBranchCorrect, IsPredCorrect, not_1_out;
  wire [31:0] CorrectPredBranch, gshare_predictor_1_predbranchdest, input_generator_1_branchdestaddress,
       input_generator_1_predpc, input_generator_1_updatepc;

  Input_Generator input_generator_1 (
    .Clock(Clock), .PredPC(input_generator_1_predpc), .UpdatePC(input_generator_1_updatepc),
    .IsBranch(input_generator_1_isbranch), .BranchTaken(input_generator_1_branchtaken),
    .BranchDestAddress(input_generator_1_branchdestaddress));
  Gshare_Predictor gshare_predictor_1 (
    .PredPC(input_generator_1_predpc), .UpdatePC(input_generator_1_updatepc),
    .IsBranch(input_generator_1_isbranch), .BranchTaken(input_generator_1_branchtaken),
    .BranchDestAddr(input_generator_1_branchdestaddress), .Clock(Clock),
    .TakeBranch(gshare_predictor_1_takebranch), .PredBranchDest(gshare_predictor_1_predbranchdest));
  Clock clock_1 (.out(Clock));
  Testing_Circuit testing_circuit_1 (
    .TakeBranch(gshare_predictor_1_takebranch), .PredBranchAddress(gshare_predictor_1_predbranchdest),
    .Clock(Clock), .IsPredCorrect(IsPredCorrect), .CorrectPred(CorrectPred),
    .IsPredBranchCorrect(IsPredBranchCorrect), .CorrectPredBranch(CorrectPredBranch), .Correct(Correct),
    .Done(Done));
  not not_1 (not_1_out, Done);
  Shift_Register #(.length(28)) shift_register_1 (
    .shift(not_1_out), .in(Correct), .clk(Clock));  // open: out, load, clr, d0, q0, d1, q1, d2, q2, d3, q3, d4, q4, d5, q5, d6, q6, d7, q7, d8, q8, d9, q9, d10, q10, d11, q11, d12, q12, d13, q13, d14, q14, d15, q15, d16, q16, d17, q17, d18, q18, d19, q19, d20, q20, d21, q21, d22, q22, d23, q23, d24, q24, d25, q25, d26, q26, d27, q27
  // Probe on IsPredCorrect
  // Probe on CorrectPred
  // Probe on IsPredBranchCorrect
  // Probe on CorrectPredBranch
  // Probe on Correct
  // Probe on Done
endmodule

module Gshare_Predictor (
  input  [31:0] PredPC,
  input  [31:0] UpdatePC,
  input  IsBranch,
  input  BranchTaken,
  input  [31:0] BranchDestAddr,
  input  Clock,
  output TakeBranch,
  output [31:0] PredBranchDest
);

  wire _0, _1, _2, _3, ADD, and_1_out, and_2_out, and_3_out, and_4_out, and_5_out, and_6_out, and_7_out,
       and_8_out, C_0, C_1, C_2, C_3, comparator_6_eq, comparator_6_gt, comparator_7_eq, comparator_7_gt,
       comparator_8_eq, comparator_8_gt, comparator_9_eq, comparator_9_gt, controlled_buffer_1_out,
       controlled_buffer_2_out, controlled_buffer_3_out, controlled_buffer_4_out, Counter_i_____2_Taken, ONE,
       or_1_out, or_2_out, or_3_out, or_4_out, or_5_out, or_6_out, or_7_out, or_8_out, or_9_out, or_10_out,
       or_11_out, or_12_out, SUB, TR_i___PC, ZERO;
  wire [1:0] _2_bit_Counter_2_q, _2_bit_Counter_3_q, _2_bit_Counter_4_q, _2_bit_Counter_q, BHR,
       bit_extender_1_out, bit_extender_2_out, bit_extender_3_out, bit_extender_4_out, Index;
  wire [31:0] Branch_Destination_Register_2_q, Branch_Destination_Register_3_q,
       Branch_Destination_Register_4_q, Branch_Destination_Register_q, multiplexer_1_out, Tag_Register_2_q,
       Tag_Register_3_q, Tag_Register_4_q, Tag_Register_q;

  Shift_Register #(.length(2)) shift_register_1 (
    .shift(IsBranch), .in(BranchTaken), .clk(Clock), .q0(BHR[1]), .q1(BHR[0]));  // open: out, load, clr, d0, d1
  and and_1 (and_1_out, IsBranch, _0);
  and and_2 (and_2_out, IsBranch, _1);
  and and_3 (and_3_out, IsBranch, _2);
  and and_4 (and_4_out, IsBranch, _3);
  and and_5 (and_5_out, IsBranch, _0);
  and and_6 (and_6_out, IsBranch, _1);
  and and_7 (and_7_out, IsBranch, _2);
  and and_8 (and_8_out, IsBranch, _3);
  Register #(.width(32)) Tag_Register (.D(UpdatePC), .en(and_1_out), .Q(Tag_Register_q), .clk(Clock));  // open: clr
  Register #(.width(32)) Tag_Register_2 (.D(UpdatePC), .en(and_2_out), .Q(Tag_Register_2_q), .clk(Clock));  // open: clr
  Register #(.width(32)) Tag_Register_3 (.D(UpdatePC), .en(and_3_out), .Q(Tag_Register_3_q), .clk(Clock));  // open: clr
  Register #(.width(32)) Tag_Register_4 (.D(UpdatePC), .en(and_4_out), .Q(Tag_Register_4_q), .clk(Clock));  // open: clr
  Register #(.width(32)) Branch_Destination_Register (
    .D(BranchDestAddr), .en(and_5_out), .Q(Branch_Destination_Register_q), .clk(Clock));  // open: clr
  Register #(.width(32)) Branch_Destination_Register_2 (
    .D(BranchDestAddr), .en(and_6_out), .Q(Branch_Destination_Register_2_q), .clk(Clock));  // open: clr
  Register #(.width(32)) Branch_Destination_Register_3 (
    .D(BranchDestAddr), .en(and_7_out), .Q(Branch_Destination_Register_3_q), .clk(Clock));  // open: clr
  Register #(.width(32)) Branch_Destination_Register_4 (
    .D(BranchDestAddr), .en(and_8_out), .Q(Branch_Destination_Register_4_q), .clk(Clock));  // open: clr
  assign Index = PredPC[1:0] ^ BHR;  // XOR_Gate xor_1, 2 bits wide
  Multiplexer #(.select(2), .width(32), .enable("false")) multiplexer_1 (
    .in0(Tag_Register_q), .in1(Tag_Register_2_q), .in2(Tag_Register_3_q), .in3(Tag_Register_4_q),
    .out(multiplexer_1_out), .sel(Index));
  Multiplexer #(.select(2), .width(32), .enable("false")) multiplexer_2 (
    .in0(Branch_Destination_Register_q), .in1(Branch_Destination_Register_2_q),
    .in2(Branch_Destination_Register_3_q), .in3(Branch_Destination_Register_4_q), .out(PredBranchDest),
    .sel(Index));
  Comparator #(.width(32), .mode("unsigned")) comparator_1 (
    .a(PredPC), .b(multiplexer_1_out), .eq(TR_i___PC));  // open: gt, lt
  Comparator #(.width(2), .mode("unsigned")) comparator_2 (.a(Index), .b(2'b00), .eq(_0));  // open: gt, lt
  Comparator #(.width(2), .mode("unsigned")) comparator_3 (.a(Index), .b(2'b01), .eq(_1));  // open: gt, lt
  Comparator #(.width(2), .mode("unsigned")) comparator_4 (.a(Index), .b(2'b10), .eq(_2));  // open: gt, lt
  Comparator #(.width(2), .mode("unsigned")) comparator_5 (.a(Index), .b(2'b11), .eq(_3));  // open: gt, lt
  and and_9 (ADD, TR_i___PC, BranchTaken);
  and and_10 (SUB, TR_i___PC, ~BranchTaken);  // AND_Gate
  and and_11 (ONE, ~TR_i___PC, BranchTaken);  // AND_Gate
  and and_12 (ZERO, ~TR_i___PC, ~BranchTaken);  // AND_Gate
  or or_1 (or_1_out, ONE, ZERO, SUB);
  assign bit_extender_1_out = {{1{1'b0}}, or_2_out};  // Bit_Extender bit_extender_1
  or or_2 (or_2_out, ONE, ~ZERO);  // OR_Gate
  or or_3 (or_3_out, ADD, SUB);
  or or_4 (or_4_out, ONE, ZERO, SUB);
  or or_5 (or_5_out, ONE, ~ZERO);  // OR_Gate
  assign bit_extender_2_out = {{1{1'b0}}, or_5_out};  // Bit_Extender bit_extender_2
  or or_6 (or_6_out, ADD, SUB);
  or or_7 (or_7_out, ONE, ZERO, SUB);
  assign bit_extender_3_out = {{1{1'b0}}, or_8_out};  // Bit_Extender bit_extender_3
  or or_8 (or_8_out, ONE, ~ZERO);  // OR_Gate
  or or_9 (or_9_out, ADD, SUB);
  or or_10 (or_10_out, ONE, ZERO, SUB);
  or or_11 (or_11_out, ONE, ~ZERO);  // OR_Gate
  assign bit_extender_4_out = {{1{1'b0}}, or_11_out};  // Bit_Extender bit_extender_4
  or or_12 (or_12_out, ADD, SUB);
  Counter #(.width(2), .max('h3), .ongoal("stay")) _2_bit_Counter (
    .load(or_1_out), .D(bit_extender_1_out), .count(or_3_out), .Q(_2_bit_Counter_q),
    .clk(controlled_buffer_1_out));  // open: carry, clr
  assign controlled_buffer_1_out = _0 ? Clock : 1'bz;  // Controlled_Buffer controlled_buffer_1
  Counter #(.width(2), .max('h3), .ongoal("stay")) _2_bit_Counter_2 (
    .load(or_4_out), .D(bit_extender_2_out), .count(or_6_out), .Q(_2_bit_Counter_2_q),
    .clk(controlled_buffer_2_out));  // open: carry, clr
  assign controlled_buffer_2_out = _1 ? Clock : 1'bz;  // Controlled_Buffer controlled_buffer_2
  Counter #(.width(2), .max('h3), .ongoal("stay")) _2_bit_Counter_3 (
    .load(or_7_out), .D(bit_extender_3_out), .count(or_9_out), .Q(_2_bit_Counter_3_q),
    .clk(controlled_buffer_3_out));  // open: carry, clr
  assign controlled_buffer_3_out = _2 ? Clock : 1'bz;  // Controlled_Buffer controlled_buffer_3
  Counter #(.width(2), .max('h3), .ongoal("stay")) _2_bit_Counter_4 (
    .load(or_10_out), .D(bit_extender_4_out), .count(or_12_out), .Q(_2_bit_Counter_4_q),
    .clk(controlled_buffer_4_out));  // open: carry, clr
  assign controlled_buffer_4_out = _3 ? Clock : 1'bz;  // Controlled_Buffer controlled_buffer_4
  Comparator #(.width(2), .mode("unsigned")) comparator_6 (
    .a(_2_bit_Counter_q), .b(2'b10), .gt(comparator_6_gt), .eq(comparator_6_eq));  // open: lt
  Comparator #(.width(2), .mode("unsigned")) comparator_7 (
    .a(_2_bit_Counter_2_q), .b(2'b10), .gt(comparator_7_gt), .eq(comparator_7_eq));  // open: lt
  Comparator #(.width(2), .mode("unsigned")) comparator_8 (
    .a(_2_bit_Counter_3_q), .b(2'b10), .gt(comparator_8_gt), .eq(comparator_8_eq));  // open: lt
  Comparator #(.width(2), .mode("unsigned")) comparator_9 (
    .a(_2_bit_Counter_4_q), .b(2'b10), .gt(comparator_9_gt), .eq(comparator_9_eq));  // open: lt
  or or_13 (C_0, comparator_6_gt, comparator_6_eq);
  or or_14 (C_1, comparator_7_gt, comparator_7_eq);
  or or_15 (C_2, comparator_8_gt, comparator_8_eq);
  or or_16 (C_3, comparator_9_gt, comparator_9_eq);
  and and_13 (TakeBranch, TR_i___PC, Counter_i_____2_Taken);
  Multiplexer #(.select(2), .enable("false")) multiplexer_3 (
    .in0(C_0), .in1(C_1), .in2(C_2), .in3(C_3), .out(Counter_i_____2_Taken), .sel(Index));

  // Other names for the same wires on the sheet: DestAddress[31:0] = BranchDestAddr; Bottom2Bits[1:0] = PredPC[1:0];
  //   PC[31:0] = PredPC; PredBranchTaken[31:0] = PredBranchDest

  // Notes on the sheet:
  //   2-bit Branch History Register
endmodule

module Input_Generator (
  input  Clock,
  output [31:0] PredPC,
  output [31:0] UpdatePC,
  output IsBranch,
  output BranchTaken,
  output [31:0] BranchDestAddress
);

  wire [7:0] counter_1_q;

  Counter #(.max('h1b), .ongoal("stay")) counter_1 (
    .count(1'b1), .Q(counter_1_q), .clk(Clock));  // open: load, D, carry, clr
  ROM #(.dataWidth(32)) rom_1 (.addr(counter_1_q), .data(PredPC));  // open: sel
  ROM #(.dataWidth(1)) rom_2 (.addr(counter_1_q), .data(IsBranch));  // open: sel
  ROM #(.dataWidth(1)) rom_3 (.addr(counter_1_q), .data(BranchTaken));  // open: sel
  ROM #(.dataWidth(32)) rom_4 (.addr(counter_1_q), .data(BranchDestAddress));  // open: sel

  assign UpdatePC = PredPC;

  // Notes on the sheet:
  //   Counter max count is 27 because there are only 28 instructions
  //   contents of rom_1 (hex, n*v repeats v):
  //   5*0 1 1 1 5 2 2 2 3 3 3 0 0 4
  //   contents of rom_2 (hex, n*v repeats v):
  //   8*1 0 8*1 0 10*1
  //   contents of rom_3 (hex, n*v repeats v):
  //   8*1 0 6*1 4*0 1 0 1 0 1 0 1 0 1
  //   contents of rom_4 (hex, n*v repeats v):
  //   5*60 5f 5f 5f 0 5 5 5 8 8 8 60 60 0 10*60
endmodule

module Testing_Circuit (
  input  TakeBranch,
  input  [31:0] PredBranchAddress,
  input  Clock,
  output IsPredCorrect,
  output CorrectPred,
  output IsPredBranchCorrect,
  output [31:0] CorrectPredBranch,
  output Correct,
  output Done
);

  wire comparator_1_eq, comparator_2_eq, DontCare, not_1_out;
  wire [7:0] Count;

  Counter #(.max('h1c), .ongoal("stay")) counter_1 (.count(1'b1), .Q(Count), .clk(Clock));  // open: load, D, carry, clr
  ROM #(.dataWidth(1)) rom_1 (.addr(Count), .data(CorrectPred));  // open: sel
  ROM #(.dataWidth(32)) rom_2 (.addr(Count), .data(CorrectPredBranch));  // open: sel
  ROM #(.dataWidth(1)) rom_3 (.addr(Count), .data(DontCare));  // open: sel
  not not_1 (not_1_out, CorrectPred);
  Comparator #(.width(1), .mode("unsigned")) comparator_1 (
    .a(TakeBranch), .b(CorrectPred), .eq(comparator_1_eq));  // open: gt, lt
  or or_1 (IsPredCorrect, comparator_1_eq, DontCare);
  Comparator #(.width(32), .mode("unsigned")) comparator_2 (
    .a(PredBranchAddress), .b(CorrectPredBranch), .eq(comparator_2_eq));  // open: gt, lt
  Comparator #(.mode("unsigned")) comparator_3 (.a(Count), .b(8'h1c), .eq(Done));  // open: gt, lt
  // Probe on Count
  or or_2 (IsPredBranchCorrect, comparator_2_eq, not_1_out, DontCare);
  and and_1 (Correct, IsPredCorrect, IsPredBranchCorrect);

  // Notes on the sheet:
  //   Correct Take Branch
  //   Correct Prediction Branch Address
  //   Don't Care
  //   contents of rom_1 (hex, n*v repeats v):
  //   4*0 1 0 0 1 0 0 0 1 0 0 1 1 9*0 1 0 1
  //   contents of rom_2 (hex, n*v repeats v):
  //   0 0 0 60 60 0 5f 5f 5f 60 5 5 60 8 8 60 5f 8 8 60 5 7*60
  //   contents of rom_3 (hex, n*v repeats v):
  //   8*0 1 8*0 1
endmodule
