// Logisim project Multi Cycle CPU.circ as structural Verilog: 6 circuits, main circuit Main
module Main (
);

  wire ALUSrcA, and_1_out, Clk, IRWrite, lorD, MemRead, MemWrite, or_1_out, PCWrite, PCWriteCond, RegWrite,
       SHAMTEnable, Zero;
  wire [1:0] ALUSrcB, MemToReg, PCSource, RegDst;
  wire [2:0] ALUOp;
  wire [3:0] NextState;
  wire [4:0] controlled_buffer_1_out, DestinationRegister, WrAddr;
  wire [5:0] Function;
  wire [7:0] multiplexer_3_out;
  wire [10:6] Immediate;
  wire [23:20] rom_1_data;
  wire [27:0] bit_extender_2_out, shifter_2_out;
  wire [31:0] alu_1_aluresult, ALUResult, bit_extender_1_out, Data1, Data2, MEMORY, multiplexer_4_out,
       multiplexer_5_out, PC, PC_Next, ram_1_data, register_file_1_rddata1, register_file_1_rddata2,
       shifter_1_out, WrData;
  wire [31:16] Instruction;

  Clock clock_1 (.out(Clk));
  and and_1 (and_1_out, Zero, PCWriteCond);
  Multiplexer #(.select(2), .width(5), .enable("false")) multiplexer_1 (
    .in0(DestinationRegister), .in1(Instruction[20:16]), .in2({5{1'b1}}), .out(WrAddr), .sel(RegDst));  // open: in3
  Multiplexer #(.select(2), .width(32), .enable("false")) multiplexer_2 (
    .in0(ALUResult), .in1(MEMORY), .in2(PC), .out(WrData), .sel(MemToReg));  // open: in3
  assign bit_extender_1_out = {{16{DestinationRegister[4]}}, {DestinationRegister, Immediate, Function}};  // Bit_Extender bit_extender_1
  or or_1 (or_1_out, PCWrite, and_1_out);
  Multiplexer #(.width(8), .enable("false")) multiplexer_3 (
    .in0(PC[9:2]), .in1(ALUResult[9:2]), .out(multiplexer_3_out), .sel(lorD));
  Shifter #(.width(32)) shifter_1 (.in(bit_extender_1_out), .\dist (5'b00010), .out(shifter_1_out));
  assign controlled_buffer_1_out = SHAMTEnable ? Immediate : 5'bz;  // Controlled_Buffer controlled_buffer_1
  Register #(.width(32)) u_PC (.D(PC_Next), .en(or_1_out), .Q(PC), .clk(Clk));  // open: clr
  Multiplexer #(.width(32), .enable("false")) multiplexer_4 (
    .in0(PC), .in1(Data1), .out(multiplexer_4_out), .sel(ALUSrcA));
  ALU alu_1 (
    .ALUCtl(ALUOp), .A(multiplexer_4_out), .B(multiplexer_5_out), .ALUResult(alu_1_aluresult), .Zero(Zero),
    .Shamt(controlled_buffer_1_out));  // open: Overflow
  Multiplexer #(.select(2), .width(32), .enable("false")) multiplexer_5 (
    .in0(Data2), .in1(32'h4), .in2(bit_extender_1_out), .in3(shifter_1_out), .out(multiplexer_5_out),
    .sel(ALUSrcB));
  RAM #(.dataWidth(32), .bus("separate")) ram_1 (
    .addr(multiplexer_3_out), .din(Data2), .data(ram_1_data), .str(MemWrite), .clk(Clk), .ld(MemRead));  // open: sel, clr
  Register #(.width(32)) IR (
    .D(ram_1_data), .en(IRWrite), .Q({Instruction, DestinationRegister, Immediate, Function}), .clk(Clk));  // open: clr
  Register #(.width(32)) MDR (.D(ram_1_data), .Q(MEMORY), .clk(Clk));  // open: en, clr
  Register_File register_file_1 (
    .WrAddr(WrAddr), .WrData(WrData), .WrReg(RegWrite), .RdAddr1(Instruction[25:21]),
    .RdAddr2(Instruction[20:16]), .RdData1(register_file_1_rddata1), .RdData2(register_file_1_rddata2),
    .Clock(Clk));
  assign bit_extender_2_out = {{2{1'b0}}, {Instruction[25:16], DestinationRegister, Immediate, Function}};  // Bit_Extender bit_extender_2
  Register #(.width(32)) B (.D(register_file_1_rddata2), .Q(Data2), .clk(Clk));  // open: en, clr
  Register #(.width(32)) ALUout (.D(alu_1_aluresult), .Q(ALUResult), .clk(Clk));  // open: en, clr
  Shifter #(.width(28)) shifter_2 (.in(bit_extender_2_out), .\dist (5'b00010), .out(shifter_2_out));
  Register #(.width(32)) A (.D(register_file_1_rddata1), .Q(Data1), .clk(Clk));  // open: en, clr
  Multiplexer #(.select(2), .width(32), .enable("false")) multiplexer_6 (
    .in0(alu_1_aluresult), .in1(ALUResult), .in2({PC[31:28], shifter_2_out}), .in3(Data1), .out(PC_Next),
    .sel(PCSource));
  ROM #(.addrWidth(16), .dataWidth(24)) rom_1 (
    .addr({Instruction[31:26], Function, NextState}),
    .data({rom_1_data, ALUOp, RegDst, RegWrite, ALUSrcA, ALUSrcB, SHAMTEnable, MemWrite, MemRead, MemToReg, IRWrite, lorD, PCWrite, PCWriteCond, PCSource}));  // open: sel
  // Probe on PC
  // Probe on RegWrite
  // Probe on WrAddr
  // Probe on WrData
  Register #(.width(4)) register_1 (.D(rom_1_data), .Q(NextState), .clk(Clk));  // open: en, clr
  // Probe on Data2
  // Probe on MemWrite
  // Probe on PCWriteCond

  // Other names for the same wires on the sheet: TopPC[3:0] = PC[31:28];
  //   Immediate (some bits) = {DestinationRegister, Function};
  //   Instruction[15:0] = {DestinationRegister, Immediate, Function};
  //   offset[25:0] = {Instruction[25:16], DestinationRegister, Immediate, Function}; OpCode[5:0] = Instruction[31:26];
  //   SHAMT[4:0] = Immediate; TargetRegister[4:0] = Instruction[20:16]; SourceRegister[4:0] = Instruction[25:21];
  //   ToRAM[7:0] = PC[9:2]

  // Notes on the sheet:
  //   contents of rom_1 (hex, n*v repeats v):
  //   120928 821800 6000a 6000b 7408a 61804 d63000 cc2000 cc0400 23000 e60110 60210 64000 6c000 6c040
  //   60000 120928 721800 6000a 6000b 7408a 61804 d63000 c62000 c60400 23000 e60110 60210 64000 6c000
  //   6c040 60000 120928 821800 6000a 6000b 7408a 61804 d63000 ce2000 ce0400 23000 e60110 60210 64000
  //   6c000 6c040 60000 120928 721800 6000a 6000b 7408a 61804 d63000 c62000 c60400 23000 e60110 60210
  //   64000 6c000 6c040 60000 120928 721800 6000a 6000b 7408a 61804 d63000 c62000 c60400 23000 e60110
  //   60210 64000 6c000 6c040 60000 120928 721800 6000a 6000b 7408a 61804 d63000 c62000 c60400 23000
  //   e60110 60210 64000 6c000 6c040 60000 120928 721800 6000a 6000b 7408a 61804 d63000 c62000 c60400
  //   23000 e60110 60210 64000 6c000 6c040 60000 120928 721800 6000a 6000b 7408a 61804 d63000 c62000
  //   c60400 23000 e60110 60210 64000 6c000 6c040 60000 120928 321800 6000a 6000b 7408a 61804 d63000
  //   c62000 c60400 23000 e60110 60210 64000 6c000 6c040 60000 120928 721800 6000a 6000b 7408a 61804
  //   d63000 c62000 c60400 23000 e60110 60210 64000 6c000 6c040 60000 120928 721800 6000a 6000b 7408a
  //   61804 d63000 c62000 c60400 23000 e60110 60210 64000 6c000 6c040 60000 120928 721800 6000a 6000b
  //   7408a 61804 d63000 c62000 c60400 23000 e60110 60210 64000 6c000 6c040 60000 120928 721800 6000a
  //   6000b 7408a 61804 d63000 c62000 c60400 23000 e60110 60210 64000 6c000 6c040 60000 120928 721800
  //   6000a 6000b 7408a 61804 d63000 c62000 c60400 23000 e60110 60210 64000 6c000 6c040 60000 120928
  //   721800 6000a 6000b 7408a 61804 d63000 c62000 c60400 23000 e60110 60210 64000 6c000 6c040 60000
  //   120928 721800 6000a 6000b 7408a 61804 d63000 c62000 c60400 23000 e60110 60210 64000 6c000 6c040
  //   60000 120928 721800 6000a 6000b 7408a 61804 d63000 c62000 c60400 23000 e60110 60210 64000 6c000
  //   6c040 60000 120928 721800 6000a 6000b 7408a 61804 d63000 c62000 c60400 23000 e60110 60210 64000
  //   6c000 6c040 60000 120928 721800 6000a 6000b 7408a 61804 d63000 c62000 c60400 23000 e60110 60210
  //   64000 6c000 6c040 60000 120928 721800 6000a 6000b 7408a 61804 d63000 c62000 c60400 23000 e60110
  //   60210 64000 6c000 6c040 60000 120928 721800 6000a 6000b 7408a 61804 d63000 c62000 c60400 23000
  //   e60110 60210 64000 6c000 6c040 60000 120928 721800 6000a 6000b 7408a 61804 d63000 c62000 c60400
  //   23000 e60110 60210 64000 6c000 6c040 60000 120928 721800 6000a 6000b 7408a 61804 d63000 c62000
  //   c60400 23000 e60110 60210 64000 6c000 6c040 60000 120928 721800 6000a 6000b 7408a 61804 d63000
  //   c62000 c60400 23000 e60110 60210 64000 6c000 6c040 60000 120928 721800 6000a 6000b 7408a 61804
  //   d63000 c62000 c60400 23000 e60110 60210 64000 6c000 6c040 60000 120928 721800 6000a 6000b 7408a
  //   61804 d63000 c62000 c60400 23000 e60110 60210 64000 6c000 6c040 60000 120928 721800 6000a 6000b
  //   7408a 61804 d63000 c62000 c60400 23000 e60110 60210 64000 6c000 6c040 60000 120928 721800 6000a
  //   6000b 7408a 61804 d63000 c62000 c60400 23000 e60110 60210 64000 6c000 6c040 60000 120928 721800
  //   6000a 6000b 7408a 61804 d63000 c62000 c60400 23000 e60110 60210 64000 6c000 6c040 60000 120928
  //   721800 6000a 6000b 7408a 61804 d63000 c62000 c60400 23000 e60110 60210 64000 6c000 6c040 60000
  //   120928 721800 6000a 6000b 7408a 61804 d63000 c62000 c60400 23000 e60110 60210 64000 6c000 6c040
  //   60000 120928 721800 6000a 6000b 7408a 61804 d63000 c62000 c60400 23000 e60110 60210 64000 6c000
  //   6c040 60000 120928 721800 6000a 6000b 7408a 61804 d63000 c22000 c60400 23000 e60110 60210 64000
  //   6c000 6c040 60000 120928 721800 6000a 6000b 7408a 61804 d63000 c62000 c60400 23000 e60110 60210
  //   64000 6c000 6c040 60000 120928 721800 6000a 6000b 7408a 61804 d63000 c62000 c60400 23000 e60110
  //   60210 64000 6c000 6c040 60000 120928 721800 6000a 6000b 7408a 61804 d63000 c62000 c60400 23000
  //   e60110 60210 64000 6c000 6c040 60000 120928 721800 6000a 6000b 7408a 61804 d63000 c02000 c60400
  //   23000 e60110 60210 64000 6c000 6c040 60000 120928 721800 6000a 6000b 7408a 61804 d63000 c42000
  //   c60400 23000 e60110 60210 64000 6c000 6c040 60000 120928 721800 6000a 6000b 7408a 61804 d63000
  //   ca2000 c60400 23000 e60110 60210 64000 6c000 6c040 60000 120928 721800 6000a 60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
endmodule

module _32_Bit_Adder_Subtractor (
  input  Add_Sub_control,
  input  [31:0] in_2,
  input  [31:0] in_3,
  output [31:0] out_4,
  output carry_out
);

  wire adder_1_cout, subtractor_1_bout;
  wire [31:0] adder_1_out, subtractor_1_out;

  Adder #(.width(32)) adder_1 (.a(in_2), .b(in_3), .out(adder_1_out), .cout(adder_1_cout));  // open: cin
  Subtractor #(.width(32)) subtractor_1 (
    .a(in_2), .b(in_3), .out(subtractor_1_out), .bout(subtractor_1_bout));  // open: bin
  Multiplexer #(.width(32), .enable("false")) multiplexer_1 (
    .in0(adder_1_out), .in1(subtractor_1_out), .out(out_4), .sel(Add_Sub_control));
  Multiplexer #(.enable("false")) multiplexer_2 (
    .in0(adder_1_cout), .in1(subtractor_1_bout), .out(carry_out), .sel(Add_Sub_control));
endmodule

module ALU (
  input  [2:0] ALUCtl,
  input  [31:0] A,
  input  [31:0] B,
  input  [4:0] Shamt,
  output [31:0] ALUResult,
  output Zero,
  output Overflow
);

  wire and_2_out, and_3_out, comparator_1_lt, not_1_out, not_2_out, or_2_out;
  wire [31:0] Add, And, LessThan, Nor, Or, ShiftLeft, ShiftRight, Sub, Xor;

  // Probe on ALUCtl
  assign Nor = ~(A | B);  // NOR_Gate nor_1, 32 bits wide
  Adder #(.width(32)) adder_1 (.a(A), .b(B), .out(Add));  // open: cin, cout
  Subtractor #(.width(32)) subtractor_1 (.a(A), .b(B), .out(Sub));  // open: bin, bout
  assign And = A & B;  // AND_Gate and_1, 32 bits wide
  assign Or = A | B;  // OR_Gate or_1, 32 bits wide
  assign Xor = A ^ B;  // XOR_Gate xor_1, 32 bits wide
  Comparator #(.width(32)) comparator_1 (.a(A), .b(B), .lt(comparator_1_lt));  // open: gt, eq
  assign LessThan = {{31{1'b0}}, comparator_1_lt};  // Bit_Extender bit_extender_1
  Shifter #(.width(32)) shifter_1 (.in(B), .\dist (Shamt), .out(ShiftLeft));
  Shifter #(.width(32), .shift("lr")) shifter_2 (.in(B), .\dist (Shamt), .out(ShiftRight));
  Multiplexer #(.select(3), .width(32), .enable("false")) multiplexer_1 (
    .in0(And), .in1(Add), .in2(Or), .in3(Sub), .in4(LessThan), .in5(Xor), .in6(ShiftLeft), .in7(ShiftRight),
    .out(ALUResult), .sel(ALUCtl));
  not not_1 (not_1_out, ALUCtl[1]);
  not not_2 (not_2_out, ALUCtl[2]);
  and and_2 (and_2_out, ALUCtl[0], not_1_out, not_2_out);
  and and_3 (and_3_out, ALUCtl[0], ALUCtl[1], not_2_out);
  Overflow_Unit overflow_unit_1 (
    .Add(and_2_out), .Sub(and_3_out), .ASign(A[31]), .BSign(B[31]), .ResultSign(ALUResult[31]),
    .Overflow(Overflow));
  or or_2 (or_2_out, ALUResult[0], ALUResult[1], ALUResult[2], ALUResult[3], ALUResult[4], ALUResult[5], ALUResult[6], ALUResult[7], ALUResult[8], ALUResult[9], ALUResult[10], ALUResult[11], ALUResult[12], ALUResult[13], ALUResult[14], ALUResult[15], ALUResult[16], ALUResult[17], ALUResult[18], ALUResult[19], ALUResult[20], ALUResult[21], ALUResult[22], ALUResult[23], ALUResult[24], ALUResult[25], ALUResult[26], ALUResult[27], ALUResult[28], ALUResult[29], ALUResult[30], ALUResult[31]);
  not not_3 (Zero, or_2_out);

  // Other names for the same wires on the sheet: ASign = A[31]; ResultSign = ALUResult[31]; BSign = B[31]
endmodule

module Register_File (
  input  [4:0] WrAddr,
  input  [31:0] WrData,
  input  WrReg,
  input  [4:0] RdAddr1,
  input  [4:0] RdAddr2,
  input  Clock,
  output [31:0] RdData1,
  output [31:0] RdData2
);

  wire WrReg0, WrReg1, WrReg2, WrReg3, WrReg4, WrReg5, WrReg6, WrReg7, WrReg8, WrReg9, WrReg10, WrReg11,
       WrReg12, WrReg13, WrReg14, WrReg15, WrReg16, WrReg17, WrReg18, WrReg19, WrReg20, WrReg21, WrReg22,
       WrReg23, WrReg24, WrReg25, WrReg26, WrReg27, WrReg28, WrReg29, WrReg30, WrReg31;
  wire [31:0] RegData1, RegData2, RegData3, RegData4, RegData5, RegData6, RegData7, RegData8, RegData9,
       RegData10, RegData11, RegData12, RegData13, RegData14, RegData15, RegData16, RegData17, RegData18,
       RegData19, RegData20, RegData21, RegData22, RegData23, RegData24, RegData25, RegData26, RegData27,
       RegData28, RegData29, RegData30, RegData31;

  Demultiplexer #(.select(5), .enable("false")) demultiplexer_1 (
    .out0(WrReg0), .out1(WrReg1), .out2(WrReg2), .out3(WrReg3), .out4(WrReg4), .out5(WrReg5), .out6(WrReg6),
    .out7(WrReg7), .out8(WrReg8), .out9(WrReg9), .out10(WrReg10), .out11(WrReg11), .out12(WrReg12),
    .out13(WrReg13), .out14(WrReg14), .out15(WrReg15), .out16(WrReg16), .out17(WrReg17), .out18(WrReg18),
    .out19(WrReg19), .out20(WrReg20), .out21(WrReg21), .out22(WrReg22), .out23(WrReg23), .out24(WrReg24),
    .out25(WrReg25), .out26(WrReg26), .out27(WrReg27), .out28(WrReg28), .out29(WrReg29), .out30(WrReg30),
    .out31(WrReg31), .in(WrReg), .sel(WrAddr));
  // Probe on RegData4
  Register #(.width(32)) Reg4 (.D(WrData), .en(WrReg4), .Q(RegData4), .clk(Clock));  // open: clr
  // Probe on RegData8
  Register #(.width(32)) Reg8 (.D(WrData), .en(WrReg8), .Q(RegData8), .clk(Clock));  // open: clr
  // Probe on RegData12
  Register #(.width(32)) Reg12 (.D(WrData), .en(WrReg12), .Q(RegData12), .clk(Clock));  // open: clr
  // Probe on RegData16
  Register #(.width(32)) Reg16 (.D(WrData), .en(WrReg16), .Q(RegData16), .clk(Clock));  // open: clr
  // Probe on RegData20
  Register #(.width(32)) Reg20 (.D(WrData), .en(WrReg20), .Q(RegData20), .clk(Clock));  // open: clr
  // Probe on RegData24
  Register #(.width(32)) Reg24 (.D(WrData), .en(WrReg24), .Q(RegData24), .clk(Clock));  // open: clr
  // Probe on RegData28
  Register #(.width(32)) Reg28 (.D(WrData), .en(WrReg28), .Q(RegData28), .clk(Clock));  // open: clr
  Register #(.width(32)) Reg1 (.D(WrData), .en(WrReg1), .Q(RegData1), .clk(Clock));  // open: clr
  Register #(.width(32)) Reg5 (.D(WrData), .en(WrReg5), .Q(RegData5), .clk(Clock));  // open: clr
  Register #(.width(32)) Reg9 (.D(WrData), .en(WrReg9), .Q(RegData9), .clk(Clock));  // open: clr
  Register #(.width(32)) Reg13 (.D(WrData), .en(WrReg13), .Q(RegData13), .clk(Clock));  // open: clr
  Register #(.width(32)) Reg17 (.D(WrData), .en(WrReg17), .Q(RegData17), .clk(Clock));  // open: clr
  Register #(.width(32)) Reg21 (.D(WrData), .en(WrReg21), .Q(RegData21), .clk(Clock));  // open: clr
  Register #(.width(32)) Reg25 (.D(WrData), .en(WrReg25), .Q(RegData25), .clk(Clock));  // open: clr
  Register #(.width(32)) Reg29 (.D(WrData), .en(WrReg29), .Q(RegData29), .clk(Clock));  // open: clr
  // Probe on RegData1
  // Probe on RegData5
  // Probe on RegData9
  // Probe on RegData13
  // Probe on RegData17
  // Probe on RegData21
  // Probe on RegData25
  // Probe on RegData29
  // Probe on RegData2
  Register #(.width(32)) Reg2 (.D(WrData), .en(WrReg2), .Q(RegData2), .clk(Clock));  // open: clr
  // Probe on RegData6
  Register #(.width(32)) Reg6 (.D(WrData), .en(WrReg6), .Q(RegData6), .clk(Clock));  // open: clr
  // Probe on RegData10
  Register #(.width(32)) Reg10 (.D(WrData), .en(WrReg10), .Q(RegData10), .clk(Clock));  // open: clr
  // Probe on RegData14
  Register #(.width(32)) Reg14 (.D(WrData), .en(WrReg14), .Q(RegData14), .clk(Clock));  // open: clr
  // Probe on RegData18
  Register #(.width(32)) Reg18 (.D(WrData), .en(WrReg18), .Q(RegData18), .clk(Clock));  // open: clr
  // Probe on RegData22
  Register #(.width(32)) Reg22 (.D(WrData), .en(WrReg22), .Q(RegData22), .clk(Clock));  // open: clr
  // Probe on RegData26
  Register #(.width(32)) Reg26 (.D(WrData), .en(WrReg26), .Q(RegData26), .clk(Clock));  // open: clr
  // Probe on RegData30
  Register #(.width(32)) Reg30 (.D(WrData), .en(WrReg30), .Q(RegData30), .clk(Clock));  // open: clr
  // Probe on RegData3
  Register #(.width(32)) Reg3 (.D(WrData), .en(WrReg3), .Q(RegData3), .clk(Clock));  // open: clr
  // Probe on RegData7
  Register #(.width(32)) Reg7 (.D(WrData), .en(WrReg7), .Q(RegData7), .clk(Clock));  // open: clr
  // Probe on RegData11
  Register #(.width(32)) Reg11 (.D(WrData), .en(WrReg11), .Q(RegData11), .clk(Clock));  // open: clr
  // Probe on RegData15
  Register #(.width(32)) Reg15 (.D(WrData), .en(WrReg15), .Q(RegData15), .clk(Clock));  // open: clr
  // Probe on RegData19
  Register #(.width(32)) Reg19 (.D(WrData), .en(WrReg19), .Q(RegData19), .clk(Clock));  // open: clr
  // Probe on RegData23
  Register #(.width(32)) Reg23 (.D(WrData), .en(WrReg23), .Q(RegData23), .clk(Clock));  // open: clr
  // Probe on RegData27
  Register #(.width(32)) Reg27 (.D(WrData), .en(WrReg27), .Q(RegData27), .clk(Clock));  // open: clr
  // Probe on RegData31
  Register #(.width(32)) Reg31 (.D(WrData), .en(WrReg31), .Q(RegData31), .clk(Clock));  // open: clr
  Multiplexer #(.select(5), .width(32), .enable("false")) multiplexer_1 (
    .in0({32{1'b0}}), .in1(RegData1), .in2(RegData2), .in3(RegData3), .in4(RegData4), .in5(RegData5),
    .in6(RegData6), .in7(RegData7), .in8(RegData8), .in9(RegData9), .in10(RegData10), .in11(RegData11),
    .in12(RegData12), .in13(RegData13), .in14(RegData14), .in15(RegData15), .in16(RegData16),
    .in17(RegData17), .in18(RegData18), .in19(RegData19), .in20(RegData20), .in21(RegData21),
    .in22(RegData22), .in23(RegData23), .in24(RegData24), .in25(RegData25), .in26(RegData26),
    .in27(RegData27), .in28(RegData28), .in29(RegData29), .in30(RegData30), .in31(RegData31), .out(RdData1),
    .sel(RdAddr1));
  Multiplexer #(.select(5), .width(32), .enable("false")) multiplexer_2 (
    .in0({32{1'b0}}), .in1(RegData1), .in2(RegData2), .in3(RegData3), .in4(RegData4), .in5(RegData5),
    .in6(RegData6), .in7(RegData7), .in8(RegData8), .in9(RegData9), .in10(RegData10), .in11(RegData11),
    .in12(RegData12), .in13(RegData13), .in14(RegData14), .in15(RegData15), .in16(RegData16),
    .in17(RegData17), .in18(RegData18), .in19(RegData19), .in20(RegData20), .in21(RegData21),
    .in22(RegData22), .in23(RegData23), .in24(RegData24), .in25(RegData25), .in26(RegData26),
    .in27(RegData27), .in28(RegData28), .in29(RegData29), .in30(RegData30), .in31(RegData31), .out(RdData2),
    .sel(RdAddr2));
endmodule

module Overflow_Unit (
  input  Add,
  input  Sub,
  input  ASign,
  input  BSign,
  input  ResultSign,
  output Overflow
);

  wire and_1_out, and_2_out, or_1_out, xnor_1_out, xor_1_out, xor_2_out;

  xnor xnor_1 (xnor_1_out, ASign, BSign);
  xor xor_1 (xor_1_out, ASign, BSign);
  and and_1 (and_1_out, xnor_1_out, Add);
  and and_2 (and_2_out, xor_1_out, Sub);
  or or_1 (or_1_out, and_1_out, and_2_out);
  xor xor_2 (xor_2_out, ResultSign, ASign);
  and and_3 (Overflow, or_1_out, xor_2_out);

  // Notes on the sheet:
  //   Overflow occurs when doing addition and sign(A) == sign(B) && sign(result) != sign(A)
  //   Or
  //   Overflow occurs when doing subtraction and sign(A) != sign(B) && sign(result) != sign(A)
endmodule

module ControlSignals (
  input  Op0,
  input  Op1,
  input  Op2,
  input  Op3,
  input  Op4,
  input  Op5,
  input  Fn0,
  input  Fn1,
  input  Fn2,
  input  Fn3,
  input  Fn4,
  input  Fn5,
  output RegDst,
  output Jump,
  output Branch,
  output MemRead,
  output MemToReg,
  output MemWrite,
  output ALUSrc,
  output RegWrite,
  output Jal,
  output Jr,
  output ALUCtl0,
  output ALUCtl1,
  output ALUCtl2
);

  wire ADD, ADDI, AND, ANDI, J, OR, ORI, SLT, SUB, XOR;

  or or_1 (RegDst, AND, ADD, OR, SUB, SLT, XOR);
  and and_1 (AND, ~Op0, ~Op1, ~Op2, ~Op3, ~Op4, ~Op5, ~Fn0, ~Fn1, Fn2, ~Fn3, ~Fn4, Fn5);  // AND_Gate
  and and_2 (ANDI, ~Op0, ~Op1, Op2, Op3, ~Op4, ~Op5);  // AND_Gate
  and and_3 (MemWrite, Op0, Op1, ~Op2, Op3, ~Op4, Op5);  // AND_Gate
  or or_2 (Jump, J, Jal);
  and and_4 (ADDI, ~Op0, ~Op1, ~Op2, Op3, ~Op4, ~Op5);  // AND_Gate
  and and_5 (Branch, ~Op0, ~Op1, Op2, ~Op3, ~Op4, ~Op5);  // AND_Gate
  and and_6 (ADD, ~Op0, ~Op1, ~Op2, ~Op3, ~Op4, ~Op5, ~Fn0, ~Fn1, ~Fn2, ~Fn3, ~Fn4, Fn5);  // AND_Gate
  or or_3 (ALUSrc, ANDI, ADDI, ORI, MemRead, MemWrite);
  and and_7 (ORI, Op0, ~Op1, Op2, Op3, ~Op4, ~Op5);  // AND_Gate
  and and_8 (J, ~Op0, Op1, ~Op2, ~Op3, ~Op4, ~Op5);  // AND_Gate
  and and_9 (OR, ~Op0, ~Op1, ~Op2, ~Op3, ~Op4, ~Op5, Fn0, ~Fn1, Fn2, ~Fn3, ~Fn4, Fn5);  // AND_Gate
  and and_10 (MemRead, Op0, Op1, ~Op2, ~Op3, ~Op4, Op5);  // AND_Gate
  and and_11 (Jal, Op0, Op1, ~Op2, ~Op3, ~Op4, ~Op5);  // AND_Gate
  or or_4 (RegWrite, AND, ADD, OR, SUB, SLT, XOR, ANDI, ADDI, ORI, MemRead, Jal);
  and and_12 (SUB, ~Op0, ~Op1, ~Op2, ~Op3, ~Op4, ~Op5, ~Fn0, Fn1, ~Fn2, ~Fn3, ~Fn4, Fn5);  // AND_Gate
  or or_5 (ALUCtl2, XOR, SLT);
  and and_13 (Jr, ~Op0, ~Op1, ~Op2, ~Op3, ~Op4, ~Op5, ~Fn0, ~Fn1, ~Fn2, Fn3, ~Fn4, ~Fn5);  // AND_Gate
  or or_6 (ALUCtl1, Branch, ORI, OR, SUB);
  and and_14 (SLT, ~Op0, ~Op1, ~Op2, ~Op3, ~Op4, ~Op5, ~Fn0, Fn1, ~Fn2, Fn3, ~Fn4, Fn5);  // AND_Gate
  or or_7 (ALUCtl0, ADD, SUB, XOR, ADDI, MemRead, MemWrite, Branch);
  and and_15 (XOR, ~Op0, ~Op1, ~Op2, ~Op3, ~Op4, ~Op5, ~Fn0, Fn1, Fn2, ~Fn3, ~Fn4, Fn5);  // AND_Gate

  assign MemToReg = MemRead;

  // Other names for the same wires on the sheet: BEQ = Branch; LW = MemRead; SW = MemWrite
endmodule
