// Logisim project Single Cycle CPU.circ as structural Verilog: 6 circuits, main circuit Main
module Main (
);

  wire ALUSrc, and_1_out, Branch, Clk, Jal, Jr, Jump, MemRead, MemToReg, MemWrite, RegDst, RegWrite, Zero;
  wire [2:0] ALUCtl;
  wire [4:0] DestinationRegister, multiplexer_1_out, WrAddr;
  wire [5:0] Function, OpCode;
  wire [7:0] bit_extender_4_out, bit_extender_5_out;
  wire [10:6] ImmediateOperand;
  wire [25:16] offset;
  wire [27:0] bit_extender_1_out, PC_4;
  wire [31:0] ALUResult, bit_extender_2_out, bit_extender_3_out, BranchAddress, Data1, Data2, JumpAddress,
       MEMORY, multiplexer_3_out, multiplexer_5_out, multiplexer_6_out, multiplexer_7_out, PC, PC_Next,
       shifter_2_out, shifter_3_out, WrData;

  assign bit_extender_1_out = {{2{1'b0}}, {offset, DestinationRegister, ImmediateOperand, Function}};  // Bit_Extender bit_extender_1
  Clock clock_1 (.out(Clk));
  Adder #(.width(32)) adder_1 (.a(PC), .b(32'h4), .out({JumpAddress[31:28], PC_4}));  // open: cin, cout
  Shifter #(.width(28)) shifter_1 (.in(bit_extender_1_out), .\dist (5'b00010), .out(JumpAddress[27:0]));
  assign bit_extender_2_out = {{16{1'b0}}, {DestinationRegister, ImmediateOperand, Function}};  // Bit_Extender bit_extender_2
  ControlSignals ControlSignals (
    .Op0(OpCode[0]), .Op1(OpCode[1]), .Op2(OpCode[2]), .Op3(OpCode[3]), .Op4(OpCode[4]), .Op5(OpCode[5]),
    .Fn0(Function[0]), .Fn1(Function[1]), .Fn2(Function[2]), .Fn3(Function[3]), .Fn4(Function[4]),
    .Fn5(Function[5]), .RegDst(RegDst), .Jump(Jump), .Branch(Branch), .MemRead(MemRead), .MemToReg(MemToReg),
    .MemWrite(MemWrite), .ALUSrc(ALUSrc), .RegWrite(RegWrite), .Jal(Jal), .Jr(Jr), .ALUCtl0(ALUCtl[0]),
    .ALUCtl1(ALUCtl[1]), .ALUCtl2(ALUCtl[2]));
  Adder #(.width(32)) adder_2 (
    .a({JumpAddress[31:28], PC_4}), .b(shifter_2_out), .out(BranchAddress));  // open: cin, cout
  Shifter #(.width(32)) shifter_2 (.in(bit_extender_2_out), .\dist (5'b00010), .out(shifter_2_out));
  Multiplexer #(.width(5), .enable("false")) multiplexer_1 (
    .in0(offset[20:16]), .in1(DestinationRegister), .out(multiplexer_1_out), .sel(RegDst));
  Multiplexer #(.width(5), .enable("false")) multiplexer_2 (
    .in0(multiplexer_1_out), .in1({5{1'b1}}), .out(WrAddr), .sel(Jal));
  Multiplexer #(.width(32), .enable("false")) multiplexer_3 (
    .in0(ALUResult), .in1(MEMORY), .out(multiplexer_3_out), .sel(MemToReg));
  Multiplexer #(.width(32), .enable("false")) multiplexer_4 (
    .in0(multiplexer_3_out), .in1({JumpAddress[31:28], PC_4}), .out(WrData), .sel(Jal));
  Multiplexer #(.width(32), .enable("false")) multiplexer_5 (
    .in0({JumpAddress[31:28], PC_4}), .in1(BranchAddress), .out(multiplexer_5_out), .sel(and_1_out));
  and and_1 (and_1_out, Zero, Branch);
  Multiplexer #(.width(32), .enable("false")) multiplexer_6 (
    .in0(multiplexer_5_out), .in1(JumpAddress), .out(multiplexer_6_out), .sel(Jump));
  // Probe on bit_extender_3_out
  Multiplexer #(.width(32), .enable("false")) multiplexer_7 (
    .in0(Data2), .in1(bit_extender_3_out), .out(multiplexer_7_out), .sel(ALUSrc));
  assign bit_extender_3_out = {{16{1'b0}}, {DestinationRegister, ImmediateOperand, Function}};  // Bit_Extender bit_extender_3
  Bit_Extender #(.in_width(32), .out_width(8)) bit_extender_4 (.in(ALUResult), .out(bit_extender_4_out));
  Shifter #(.width(32), .shift("lr")) shifter_3 (.in(PC), .\dist (5'b00010), .out(shifter_3_out));
  Bit_Extender #(.in_width(32), .out_width(8)) bit_extender_5 (.in(shifter_3_out), .out(bit_extender_5_out));
  Multiplexer #(.width(32), .enable("false")) multiplexer_8 (
    .in0(multiplexer_6_out), .in1(Data1), .out(PC_Next), .sel(Jr));
  // Probe on Data1
  ALU alu_1 (
    .ALUCtl(ALUCtl), .A(Data1), .B(multiplexer_7_out), .ALUResult(ALUResult), .Zero(Zero), .Shamt({5{1'b0}}));  // open: Overflow
  Register_File register_file_1 (
    .WrAddr(WrAddr), .WrData(WrData), .WrReg(RegWrite), .RdAddr1(offset[25:21]), .RdAddr2(offset[20:16]),
    .RdData1(Data1), .RdData2(Data2), .Clock(Clk));
  // Probe on multiplexer_7_out
  RAM #(.dataWidth(32), .bus("separate")) ram_1 (
    .addr(bit_extender_4_out), .din(Data2), .data(MEMORY), .str(MemWrite), .clk(Clk), .ld(MemRead));  // open: sel, clr
  ROM #(.dataWidth(32)) rom_1 (
    .addr(bit_extender_5_out), .data({OpCode, offset, DestinationRegister, ImmediateOperand, Function}));  // open: sel
  Register #(.width(32)) u_PC (.D(PC_Next), .Q(PC), .clk(Clk));  // open: en, clr
  // Probe on Data1
  // Probe on Data2
  // Probe on PC
  // Probe on Branch
  // Probe on Jump
  // Probe on Jal
  // Probe on Jr
  // Probe on WrData
  // Probe on Data2
  // Probe on RegWrite
  // Probe on WrAddr
  // Probe on MemWrite

  // Other names for the same wires on the sheet: ImmediateOperand (some bits) = {DestinationRegister, Function};
  //   offset[15:0] = {DestinationRegister, ImmediateOperand, Function}; ShiftAmount[4:0] = ImmediateOperand;
  //   TargetRegister[4:0] = offset[20:16]; SourceRegister[4:0] = offset[25:21]; PC_4[31:28] = JumpAddress[31:28]

  // Notes on the sheet:
  //   contents of rom_1 (hex, n*v repeats v):
  //   20010008 34220005 3043ffff 612020 832822 223024 c33826 aca40064 8ca80064 22482a 1265025 c00000d
  //   200b0001 23ff0018 10c00003 a13022 800000e 200c0001 3e00008 200d0001 200e0001
endmodule

module _32_Bit_Adder_Subtractor (
  input  Add_Sub_control,
  input  [31:0] in_2,
  input  [31:0] in_3,
  output [31:0] out_4,
  output carry_out
);

  wire adder_1_cout, subtractor_1_bout;
  wire [31:0] adder_1_out, subtractor_1_out;

  Adder #(.width(32)) adder_1 (.a(in_2), .b(in_3), .out(adder_1_out), .cout(adder_1_cout));  // open: cin
  Subtractor #(.width(32)) subtractor_1 (
    .a(in_2), .b(in_3), .out(subtractor_1_out), .bout(subtractor_1_bout));  // open: bin
  Multiplexer #(.width(32), .enable("false")) multiplexer_1 (
    .in0(adder_1_out), .in1(subtractor_1_out), .out(out_4), .sel(Add_Sub_control));
  Multiplexer #(.enable("false")) multiplexer_2 (
    .in0(adder_1_cout), .in1(subtractor_1_bout), .out(carry_out), .sel(Add_Sub_control));
endmodule

module ALU (
  input  [2:0] ALUCtl,
  input  [31:0] A,
  input  [31:0] B,
  input  [4:0] Shamt,
  output [31:0] ALUResult,
  output Zero,
  output Overflow
);

  wire and_2_out, and_3_out, comparator_1_lt, not_1_out, not_2_out, or_2_out;
  wire [31:0] Add, And, LessThan, Nor, Or, ShiftLeft, ShiftRight, Sub, Xor;

  // Probe on ALUCtl
  assign Nor = ~(A | B);  // NOR_Gate nor_1, 32 bits wide
  Adder #(.width(32)) adder_1 (.a(A), .b(B), .out(Add));  // open: cin, cout
  Subtractor #(.width(32)) subtractor_1 (.a(A), .b(B), .out(Sub));  // open: bin, bout
  assign And = A & B;  // AND_Gate and_1, 32 bits wide
  assign Or = A | B;  // OR_Gate or_1, 32 bits wide
  assign Xor = A ^ B;  // XOR_Gate xor_1, 32 bits wide
  Comparator #(.width(32)) comparator_1 (.a(A), .b(B), .lt(comparator_1_lt));  // open: gt, eq
  assign LessThan = {{31{1'b0}}, comparator_1_lt};  // Bit_Extender bit_extender_1
  Shifter #(.width(32)) shifter_1 (.in(B), .\dist (Shamt), .out(ShiftLeft));
  Shifter #(.width(32), .shift("lr")) shifter_2 (.in(B), .\dist (Shamt), .out(ShiftRight));
  Multiplexer #(.select(3), .width(32), .enable("false")) multiplexer_1 (
    .in0(And), .in1(Add), .in2(Or), .in3(Sub), .in4(LessThan), .in5(Xor), .in6(ShiftLeft), .in7(ShiftRight),
    .out(ALUResult), .sel(ALUCtl));
  not not_1 (not_1_out, ALUCtl[1]);
  not not_2 (not_2_out, ALUCtl[2]);
  and and_2 (and_2_out, ALUCtl[0], not_1_out, not_2_out);
  and and_3 (and_3_out, ALUCtl[0], ALUCtl[1], not_2_out);
  Overflow_Unit overflow_unit_1 (
    .Add(and_2_out), .Sub(and_3_out), .ASign(A[31]), .BSign(B[31]), .ResultSign(ALUResult[31]),
    .Overflow(Overflow));
  not not_3 (Zero, or_2_out);
  or or_2 (or_2_out, ALUResult[0], ALUResult[1], ALUResult[2], ALUResult[3], ALUResult[4], ALUResult[5], ALUResult[6], ALUResult[7], ALUResult[8], ALUResult[9], ALUResult[10], ALUResult[11], ALUResult[12], ALUResult[13], ALUResult[14], ALUResult[15], ALUResult[16], ALUResult[17], ALUResult[18], ALUResult[19], ALUResult[20], ALUResult[21], ALUResult[22], ALUResult[23], ALUResult[24], ALUResult[25], ALUResult[26], ALUResult[27], ALUResult[28], ALUResult[29], ALUResult[30], ALUResult[31]);

  // Other names for the same wires on the sheet: ASign = A[31]; ResultSign = ALUResult[31]; BSign = B[31]
endmodule

module Register_File (
  input  [4:0] WrAddr,
  input  [31:0] WrData,
  input  WrReg,
  input  [4:0] RdAddr1,
  input  [4:0] RdAddr2,
  input  Clock,
  output [31:0] RdData1,
  output [31:0] RdData2
);

  wire WrReg0, WrReg1, WrReg2, WrReg3, WrReg4, WrReg5, WrReg6, WrReg7, WrReg8, WrReg9, WrReg10, WrReg11,
       WrReg12, WrReg13, WrReg14, WrReg15, WrReg16, WrReg17, WrReg18, WrReg19, WrReg20, WrReg21, WrReg22,
       WrReg23, WrReg24, WrReg25, WrReg26, WrReg27, WrReg28, WrReg29, WrReg30, WrReg31;
  wire [31:0] RegData1, RegData2, RegData3, RegData4, RegData5, RegData6, RegData7, RegData8, RegData9,
       RegData10, RegData11, RegData12, RegData13, RegData14, RegData15, RegData16, RegData17, RegData18,
       RegData19, RegData20, RegData21, RegData22, RegData23, RegData24, RegData25, RegData26, RegData27,
       RegData28, RegData29, RegData30, RegData31;

  Demultiplexer #(.select(5), .enable("false")) demultiplexer_1 (
    .out0(WrReg0), .out1(WrReg1), .out2(WrReg2), .out3(WrReg3), .out4(WrReg4), .out5(WrReg5), .out6(WrReg6),
    .out7(WrReg7), .out8(WrReg8), .out9(WrReg9), .out10(WrReg10), .out11(WrReg11), .out12(WrReg12),
    .out13(WrReg13), .out14(WrReg14), .out15(WrReg15), .out16(WrReg16), .out17(WrReg17), .out18(WrReg18),
    .out19(WrReg19), .out20(WrReg20), .out21(WrReg21), .out22(WrReg22), .out23(WrReg23), .out24(WrReg24),
    .out25(WrReg25), .out26(WrReg26), .out27(WrReg27), .out28(WrReg28), .out29(WrReg29), .out30(WrReg30),
    .out31(WrReg31), .in(WrReg), .sel(WrAddr));
  // Probe on RegData4
  Register #(.width(32)) Reg4 (.D(WrData), .en(WrReg4), .Q(RegData4), .clk(Clock));  // open: clr
  // Probe on RegData8
  Register #(.width(32)) Reg8 (.D(WrData), .en(WrReg8), .Q(RegData8), .clk(Clock));  // open: clr
  // Probe on RegData12
  Register #(.width(32)) Reg12 (.D(WrData), .en(WrReg12), .Q(RegData12), .clk(Clock));  // open: clr
  // Probe on RegData16
  Register #(.width(32)) Reg16 (.D(WrData), .en(WrReg16), .Q(RegData16), .clk(Clock));  // open: clr
  // Probe on RegData20
  Register #(.width(32)) Reg20 (.D(WrData), .en(WrReg20), .Q(RegData20), .clk(Clock));  // open: clr
  // Probe on RegData24
  Register #(.width(32)) Reg24 (.D(WrData), .en(WrReg24), .Q(RegData24), .clk(Clock));  // open: clr
  // Probe on RegData28
  Register #(.width(32)) Reg28 (.D(WrData), .en(WrReg28), .Q(RegData28), .clk(Clock));  // open: clr
  Register #(.width(32)) Reg1 (.D(WrData), .en(WrReg1), .Q(RegData1), .clk(Clock));  // open: clr
  Register #(.width(32)) Reg5 (.D(WrData), .en(WrReg5), .Q(RegData5), .clk(Clock));  // open: clr
  Register #(.width(32)) Reg9 (.D(WrData), .en(WrReg9), .Q(RegData9), .clk(Clock));  // open: clr
  Register #(.width(32)) Reg13 (.D(WrData), .en(WrReg13), .Q(RegData13), .clk(Clock));  // open: clr
  Register #(.width(32)) Reg17 (.D(WrData), .en(WrReg17), .Q(RegData17), .clk(Clock));  // open: clr
  Register #(.width(32)) Reg21 (.D(WrData), .en(WrReg21), .Q(RegData21), .clk(Clock));  // open: clr
  Register #(.width(32)) Reg25 (.D(WrData), .en(WrReg25), .Q(RegData25), .clk(Clock));  // open: clr
  Register #(.width(32)) Reg29 (.D(WrData), .en(WrReg29), .Q(RegData29), .clk(Clock));  // open: clr
  // Probe on RegData1
  // Probe on RegData5
  // Probe on RegData9
  // Probe on RegData13
  // Probe on RegData17
  // Probe on RegData21
  // Probe on RegData25
  // Probe on RegData29
  // Probe on RegData2
  Register #(.width(32)) Reg2 (.D(WrData), .en(WrReg2), .Q(RegData2), .clk(Clock));  // open: clr
  // Probe on RegData6
  Register #(.width(32)) Reg6 (.D(WrData), .en(WrReg6), .Q(RegData6), .clk(Clock));  // open: clr
  // Probe on RegData10
  Register #(.width(32)) Reg10 (.D(WrData), .en(WrReg10), .Q(RegData10), .clk(Clock));  // open: clr
  // Probe on RegData14
  Register #(.width(32)) Reg14 (.D(WrData), .en(WrReg14), .Q(RegData14), .clk(Clock));  // open: clr
  // Probe on RegData18
  Register #(.width(32)) Reg18 (.D(WrData), .en(WrReg18), .Q(RegData18), .clk(Clock));  // open: clr
  // Probe on RegData22
  Register #(.width(32)) Reg22 (.D(WrData), .en(WrReg22), .Q(RegData22), .clk(Clock));  // open: clr
  // Probe on RegData26
  Register #(.width(32)) Reg26 (.D(WrData), .en(WrReg26), .Q(RegData26), .clk(Clock));  // open: clr
  // Probe on RegData30
  Register #(.width(32)) Reg30 (.D(WrData), .en(WrReg30), .Q(RegData30), .clk(Clock));  // open: clr
  // Probe on RegData3
  Register #(.width(32)) Reg3 (.D(WrData), .en(WrReg3), .Q(RegData3), .clk(Clock));  // open: clr
  // Probe on RegData7
  Register #(.width(32)) Reg7 (.D(WrData), .en(WrReg7), .Q(RegData7), .clk(Clock));  // open: clr
  // Probe on RegData11
  Register #(.width(32)) Reg11 (.D(WrData), .en(WrReg11), .Q(RegData11), .clk(Clock));  // open: clr
  // Probe on RegData15
  Register #(.width(32)) Reg15 (.D(WrData), .en(WrReg15), .Q(RegData15), .clk(Clock));  // open: clr
  // Probe on RegData19
  Register #(.width(32)) Reg19 (.D(WrData), .en(WrReg19), .Q(RegData19), .clk(Clock));  // open: clr
  // Probe on RegData23
  Register #(.width(32)) Reg23 (.D(WrData), .en(WrReg23), .Q(RegData23), .clk(Clock));  // open: clr
  // Probe on RegData27
  Register #(.width(32)) Reg27 (.D(WrData), .en(WrReg27), .Q(RegData27), .clk(Clock));  // open: clr
  // Probe on RegData31
  Register #(.width(32)) Reg31 (.D(WrData), .en(WrReg31), .Q(RegData31), .clk(Clock));  // open: clr
  Multiplexer #(.select(5), .width(32), .enable("false")) multiplexer_1 (
    .in0({32{1'b0}}), .in1(RegData1), .in2(RegData2), .in3(RegData3), .in4(RegData4), .in5(RegData5),
    .in6(RegData6), .in7(RegData7), .in8(RegData8), .in9(RegData9), .in10(RegData10), .in11(RegData11),
    .in12(RegData12), .in13(RegData13), .in14(RegData14), .in15(RegData15), .in16(RegData16),
    .in17(RegData17), .in18(RegData18), .in19(RegData19), .in20(RegData20), .in21(RegData21),
    .in22(RegData22), .in23(RegData23), .in24(RegData24), .in25(RegData25), .in26(RegData26),
    .in27(RegData27), .in28(RegData28), .in29(RegData29), .in30(RegData30), .in31(RegData31), .out(RdData1),
    .sel(RdAddr1));
  Multiplexer #(.select(5), .width(32), .enable("false")) multiplexer_2 (
    .in0({32{1'b0}}), .in1(RegData1), .in2(RegData2), .in3(RegData3), .in4(RegData4), .in5(RegData5),
    .in6(RegData6), .in7(RegData7), .in8(RegData8), .in9(RegData9), .in10(RegData10), .in11(RegData11),
    .in12(RegData12), .in13(RegData13), .in14(RegData14), .in15(RegData15), .in16(RegData16),
    .in17(RegData17), .in18(RegData18), .in19(RegData19), .in20(RegData20), .in21(RegData21),
    .in22(RegData22), .in23(RegData23), .in24(RegData24), .in25(RegData25), .in26(RegData26),
    .in27(RegData27), .in28(RegData28), .in29(RegData29), .in30(RegData30), .in31(RegData31), .out(RdData2),
    .sel(RdAddr2));
endmodule

module Overflow_Unit (
  input  Add,
  input  Sub,
  input  ASign,
  input  BSign,
  input  ResultSign,
  output Overflow
);

  wire and_1_out, and_2_out, or_1_out, xnor_1_out, xor_1_out, xor_2_out;

  xnor xnor_1 (xnor_1_out, ASign, BSign);
  xor xor_1 (xor_1_out, ASign, BSign);
  and and_1 (and_1_out, xnor_1_out, Add);
  and and_2 (and_2_out, xor_1_out, Sub);
  or or_1 (or_1_out, and_1_out, and_2_out);
  xor xor_2 (xor_2_out, ResultSign, ASign);
  and and_3 (Overflow, or_1_out, xor_2_out);

  // Notes on the sheet:
  //   Overflow occurs when doing addition and sign(A) == sign(B) && sign(result) != sign(A)
  //   Or
  //   Overflow occurs when doing subtraction and sign(A) != sign(B) && sign(result) != sign(A)
endmodule

module ControlSignals (
  input  Op0,
  input  Op1,
  input  Op2,
  input  Op3,
  input  Op4,
  input  Op5,
  input  Fn0,
  input  Fn1,
  input  Fn2,
  input  Fn3,
  input  Fn4,
  input  Fn5,
  output RegDst,
  output Jump,
  output Branch,
  output MemRead,
  output MemToReg,
  output MemWrite,
  output ALUSrc,
  output RegWrite,
  output Jal,
  output Jr,
  output ALUCtl0,
  output ALUCtl1,
  output ALUCtl2
);

  wire ADD, ADDI, AND, ANDI, J, OR, ORI, SLT, SUB, XOR;

  or or_1 (RegDst, AND, ADD, OR, SUB, SLT, XOR);
  and and_1 (AND, ~Op0, ~Op1, ~Op2, ~Op3, ~Op4, ~Op5, ~Fn0, ~Fn1, Fn2, ~Fn3, ~Fn4, Fn5);  // AND_Gate
  and and_2 (ANDI, ~Op0, ~Op1, Op2, Op3, ~Op4, ~Op5);  // AND_Gate
  and and_3 (MemWrite, Op0, Op1, ~Op2, Op3, ~Op4, Op5);  // AND_Gate
  or or_2 (Jump, J, Jal);
  and and_4 (ADDI, ~Op0, ~Op1, ~Op2, Op3, ~Op4, ~Op5);  // AND_Gate
  and and_5 (Branch, ~Op0, ~Op1, Op2, ~Op3, ~Op4, ~Op5);  // AND_Gate
  and and_6 (ADD, ~Op0, ~Op1, ~Op2, ~Op3, ~Op4, ~Op5, ~Fn0, ~Fn1, ~Fn2, ~Fn3, ~Fn4, Fn5);  // AND_Gate
  or or_3 (ALUSrc, ANDI, ADDI, ORI, MemRead, MemWrite);
  and and_7 (ORI, Op0, ~Op1, Op2, Op3, ~Op4, ~Op5);  // AND_Gate
  and and_8 (J, ~Op0, Op1, ~Op2, ~Op3, ~Op4, ~Op5);  // AND_Gate
  and and_9 (OR, ~Op0, ~Op1, ~Op2, ~Op3, ~Op4, ~Op5, Fn0, ~Fn1, Fn2, ~Fn3, ~Fn4, Fn5);  // AND_Gate
  and and_10 (MemRead, Op0, Op1, ~Op2, ~Op3, ~Op4, Op5);  // AND_Gate
  and and_11 (Jal, Op0, Op1, ~Op2, ~Op3, ~Op4, ~Op5);  // AND_Gate
  or or_4 (RegWrite, AND, ADD, OR, SUB, SLT, XOR, ANDI, ADDI, ORI, MemRead, Jal);
  and and_12 (SUB, ~Op0, ~Op1, ~Op2, ~Op3, ~Op4, ~Op5, ~Fn0, Fn1, ~Fn2, ~Fn3, ~Fn4, Fn5);  // AND_Gate
  or or_5 (ALUCtl2, XOR, SLT);
  and and_13 (Jr, ~Op0, ~Op1, ~Op2, ~Op3, ~Op4, ~Op5, ~Fn0, ~Fn1, ~Fn2, Fn3, ~Fn4, ~Fn5);  // AND_Gate
  or or_6 (ALUCtl1, Branch, ORI, OR, SUB);
  and and_14 (SLT, ~Op0, ~Op1, ~Op2, ~Op3, ~Op4, ~Op5, ~Fn0, Fn1, ~Fn2, Fn3, ~Fn4, Fn5);  // AND_Gate
  or or_7 (ALUCtl0, ADD, SUB, XOR, ADDI, MemRead, MemWrite, Branch);
  and and_15 (XOR, ~Op0, ~Op1, ~Op2, ~Op3, ~Op4, ~Op5, ~Fn0, Fn1, Fn2, ~Fn3, ~Fn4, Fn5);  // AND_Gate

  assign MemToReg = MemRead;

  // Other names for the same wires on the sheet: BEQ = Branch; LW = MemRead; SW = MemWrite
endmodule
